# Fritzing sketch fritzing (saved by Fritzing 1.0.8)
circuit board: 5.15cm x 1.625cm

parts:
  MX1 = Cherry MX Keyswitch Simple
  J2 = female pin header, 3 pins [form="♀ (female)"]
  IN = female pin header, 4 pins [form="♀ (female)"]

nets:
  N1: MX1.pin_1, IN.pin2
  GND: MX1.pin_2, J2.pin1, IN.pin1
  N2: J2.pin2, IN.pin3
  N3: J2.pin3, IN.pin4

notes:
  5v
  GND
  BTN
  LED

custom parts:
  Cherry MX Keyswitch Simple: Cherry MX Keyswitch button for keyboards
